// Logisim project simple_alu.circ as structural Verilog: 1 circuit, main circuit main
module main (
  input  [7:0] a,
  input  [7:0] b,
  input  btnC,
  input  btnD,
  input  btnR,
  input  btnL,
  input  btnU,
  output [7:0] led,
  output hc,
  output acr,
  output avr
);

  wire adder_1_cout, adder_2_cout, and_2_out, and_3_out, and_4_out, and_5_out, and_7_out, and_8_out,
       bitselector_1_out, bitselector_2_out, bitselector_3_out, bitselector_4_out, not_1_out, not_2_out,
       not_3_out, or_2_out, undriven;
  wire [2:0] priority_encoder_1_out;
  wire [3:0] adder_1_out, adder_2_out;
  wire [7:0] and_1_out, multiplexer_1_out, or_1_out, shifter_1_out, xor_1_out;

  // NoConnect on nothing
  Priority_Encoder priority_encoder_1 (
    .in0(btnC), .in1(btnD), .in2(btnR), .in3(btnL), .in4(btnU), .in5(1'b0), .in6(1'b0), .in7(1'b0),
    .out(priority_encoder_1_out), .en_in(1'b1));
  Shifter #(.shift("lr")) shifter_1 (.in(b), .\dist (3'b001), .out(shifter_1_out));
  assign xor_1_out = b ^ a;  // XOR_Gate xor_1, 8 bits wide
  assign or_1_out = b | a;  // OR_Gate or_1, 8 bits wide
  assign and_1_out = b & a;  // AND_Gate and_1, 8 bits wide
  BitSelector bitselector_1 (.in(b), .out(bitselector_1_out), .sel(3'b000));
  and and_2 (and_2_out, bitselector_2_out, bitselector_3_out);
  BitSelector bitselector_2 (.in(a), .out(bitselector_2_out), .sel(3'b111));
  not not_1 (not_1_out, bitselector_2_out);
  BitSelector bitselector_3 (.in(b), .out(bitselector_3_out), .sel(3'b111));
  not not_2 (not_2_out, bitselector_3_out);
  BitSelector bitselector_4 (.in({adder_2_out, adder_1_out}), .out(bitselector_4_out), .sel(3'b111));
  not not_3 (not_3_out, bitselector_4_out);
  and and_3 (and_3_out, not_3_out, and_2_out);
  and and_4 (and_4_out, bitselector_4_out, and_5_out);
  and and_5 (and_5_out, not_1_out, not_2_out);
  Adder #(.width(4)) adder_1 (.a(a[3:0]), .b(b[3:0]), .out(adder_1_out), .cin(1'b0), .cout(adder_1_cout));
  Adder #(.width(4)) adder_2 (.a(a[7:4]), .b(b[7:4]), .out(adder_2_out), .cin(adder_1_cout), .cout(adder_2_cout));
  or or_2 (or_2_out, and_3_out, and_4_out);
  Multiplexer #(.select(3), .width(8)) multiplexer_1 (
    .in0(shifter_1_out), .in1(xor_1_out), .in2(or_1_out), .in3(and_1_out), .in4({adder_2_out, adder_1_out}),
    .in5({8{1'b0}}), .in6({8{1'b0}}), .in7({8{1'b0}}), .out(multiplexer_1_out), .sel(priority_encoder_1_out));
  and and_6 (hc, adder_1_cout, btnU);
  and and_7 (and_7_out, btnU, adder_2_cout);
  and and_8 (and_8_out, bitselector_1_out, btnC);
  and and_9 (avr, btnU, or_2_out);
  Multiplexer #(.width(8)) multiplexer_2 (.in0(multiplexer_1_out), .in1({8{1'b0}}), .out(led), .sel(undriven));
  or or_3 (acr, and_7_out, and_8_out);
endmodule
